# Fritzing sketch LCD_Wiring (saved by Fritzing 0.9.6b)
breadboards: 1

parts:
  Mod1 = Raspberry Pi 4B
  LCD1 = LCD screen
  R1 = TRIMPOT [package=trimpot_pth_s3_lock]
  Q1 = NPN-Transistor [package="TO92 [THT]"]
  Q2 = PNP-Transistor [package="TO92 [THT]"]
  R2 = Resistor [tolerance=±5% power=0.25 resistance=10k package=THT]
  R3 = Resistor [tolerance=±5% power=0.25 resistance=1.2k package=THT]
  R4 = Resistor [tolerance=±5% power=0.25 resistance=10k package=THT]
  R5 = Resistor [tolerance=±5% power=0.25 resistance=1.2k package=THT]

nets:
  N1: Mod1.GPIO2, LCD1.RS
  5V: Mod1.5V, LCD1.VDD, R1.CW, Q2.E, R2.Pin_0
  N2: Mod1.GPIO3, R5.Pin_1
  GND: Mod1.GND, LCD1.VSS, LCD1.R/W, LCD1.LED-, R1.CCW, Q1.E, R4.Pin_0
  N3: Mod1.GPIO4, LCD1.E
  N4: Mod1.GPIO27, LCD1.DB4
  N5: Mod1.GPIO22, LCD1.DB5
  N6: Mod1.GPIO23, LCD1.DB6
  N7: Mod1.GPIO24, LCD1.DB7
  N8: LCD1.V0, R1.WIPER
  N9: LCD1.LED+, Q2.C
  N10: Q1.B, R4.Pin_1, R5.Pin_0
  N11: Q1.C, R2.Pin_1, R3.Pin_0
  N12: Q2.B, R3.Pin_1
