# Fritzing sketch LCD_Wiring_Matrix_Display (saved by Fritzing 1.0.1rc)
breadboards: 2
stripboards: 1

parts:
  RPi1 = Raspberry Pi 4B
  Q1 = NPN-Transistor [package="TO92 [THT]"]
  Q2 = PNP-Transistor [package="TO92 [THT]"]
  R2 = Resistor [tolerance=±5% power=0.25 resistance=10k package=THT]
  R3 = Resistor [tolerance=±5% power=0.25 resistance=1.2k package=THT]
  R4 = Resistor [tolerance=±5% power=0.25 resistance=10k package=THT]
  GLCD_128x1 = 128 x 64 Graphic LCD
  J1 = JST-03JQ-BT [part_number=JST-JQ-BT package=THT]
  J2 = JST-03JQ-BT [part_number=JST-JQ-BT package=THT]
  R5 = resistor-upright [tolerance=±5% resistance=1.2k]
  R1 = TRIMPOT [knob_status=50% package=trimpot_pth_s3_lock]
  RPi2 = Raspberry Pi 4B
  R6 = TRIMPOT [knob_status=50% package=trimpot_pth_s3_lock]
  J3 = JST-03JQ-BT [part_number=JST-JQ-BT package=THT]
  S2 = Square Pushbutton
  LED1 = LED - 5mm [color="Red (633nm)" current=0.030 package="5 mm [THT]"]
  J4 = JST-03JQ-BT [part_number=JST-JQ-BT package=THT]
  Q3 = NPN-Transistor [package="TO92 [THT]"]
  Q4 = PNP-Transistor [package="TO92 [THT]"]
  R7 = Resistor [tolerance=±5% power=0.25 resistance=10k package=THT]
  R8 = Resistor [tolerance=±5% power=0.25 resistance=10k package=THT]
  R9 = Resistor [tolerance=±5% power=0.25 resistance=1.2k package=THT]
  R11 = Resistor [tolerance=±5% power=0.25 resistance=1.2k package=THT]
  J5 = JST-03JQ-BT [part_number=JST-JQ-BT package=THT]
  J6 = JST-03JQ-BT [part_number=JST-JQ-BT package=THT]

nets:
  N1: RPi1.GPIO2, GLCD_128x1.4_D/I
  N2: RPi1.5V, Q2.E, R2.Pin_0, GLCD_128x1.2_Vdd, J1.pin2, R1.CW
  N3: RPi1.GPIO3, GLCD_128x1.5_R/W
  N4: RPi1.GND, Q1.E, R4.Pin_0, GLCD_128x1.1_Vss, GLCD_128x1.18_Vout, GLCD_128x1.20_K(-), J1.pin1, J2.pin2, R1.CCW
  N5: RPi1.GPIO4, GLCD_128x1.6_Enable
  N6: RPi1.GPIO14, GLCD_128x1.15_CS1
  N7: RPi1.GPIO15, GLCD_128x1.16_CS2
  N8: RPi1.GPIO17, J6.pin1
  N9: RPi1.GPIO18, GLCD_128x1.17_RST
  N10: RPi1.GPIO27, J6.pin2
  N11: RPi1.GPIO22, R5.connector0, J6.pin3
  N12: RPi1.GPIO25, GLCD_128x1.7_DB0
  N13: RPi1.GPIO8, GLCD_128x1.8_DB1
  N14: RPi1.GPIO7, GLCD_128x1.9_BD2
  N15: RPi1.ID_SD, GLCD_128x1.11_DB4
  N16: RPi1.ID_SC, GLCD_128x1.10_DB3
  N17: RPi1.GPIO5, GLCD_128x1.12_DB5
  N18: RPi1.GPIO6, GLCD_128x1.13_DB6
  N19: RPi1.GPIO13, GLCD_128x1.14_DB7
  N20: Q1.B, R4.Pin_1, R5.connector1
  N21: Q1.C, R2.Pin_1, R3.Pin_0
  N22: Q2.B, R3.Pin_1
  N23: Q2.C, GLCD_128x1.19_A(+), J2.pin1
  N24: GLCD_128x1.3_Vo, J1.pin3, R1.WIPER
  N25: RPi2.5V, R6.CCW, J3.pin1, Q4.E, R8.Pin_1
  N26: RPi2.GND, R6.CW, J3.pin2, S2.leg1, LED1.cathode, Q3.E, R7.Pin_0, J5.pin2
  N27: RPi2.GPIO17, J4.pin3, R9.Pin_1
  N28: RPi2.GPIO27, LED1.anode, J4.pin2
  N29: RPi2.GPIO22, S2.leg0, J4.pin1
  N30: R6.WIPER, J3.pin3
  N31: Q3.B, R7.Pin_1, R9.Pin_0
  N32: Q3.C, R8.Pin_0, R11.Pin_0
  N33: Q4.B, R11.Pin_1
  N34: Q4.C, J5.pin1

notes:
  Wire link lengths are accurate except W24-U24 and X25-V25. W11-A11 and X16-A16 are closer to valley than on physical stripboard due to model inequivalence.
